# Fritzing sketch sketch (saved by Fritzing 0.9.3b)
breadboards: 1

parts:
  Bauteil1 = Arduino Pro Micro (Clone)
  U1 = SUP500F [package=sup500f]

nets:
  N1: Bauteil1.TXO, U1.GND
  N2: Bauteil1.RXI, U1.TX-O
  N3: Bauteil1.GND, U1.RX-I
  VCC: Bauteil1.VCC, U1.VCC
  N4: U1.VBAT, U1.PPS, U1.PSEL
